// Logisim project atom_mul.circ as structural Verilog: 1 circuit, main circuit full_mul
module full_mul (
  input  A,
  input  B,
  input  C_in,
  input  P,
  output S,
  output C_out
);

  wire and_1_out, and_2_out, and_3_out, xor_1_out;

  and and_1 (and_1_out, A, B);
  xor xor_1 (xor_1_out, P, and_1_out);
  xor xor_2 (S, xor_1_out, C_in);
  and and_2 (and_2_out, xor_1_out, C_in);
  and and_3 (and_3_out, P, and_1_out);
  or or_1 (C_out, and_2_out, and_3_out);
endmodule
