// Logisim project atom_mul_simple.circ as structural Verilog: 1 circuit, main circuit full_mul
module full_mul (
  input  A,
  input  B,
  input  P,
  input  C_in,
  output S,
  output C_out
);

  wire and_1_out;

  and and_1 (and_1_out, A, B);
  half_adder half_adder_1 (.B(P), .A(and_1_out), .S(S), .C_out(C_out));
endmodule
