// Logisim project atom_sum.circ as structural Verilog: 2 circuits, main circuit half_adder
module half_adder (
  input  A,
  input  B,
  output S,
  output C_out
);

  xor xor_1 (S, B, A);
  and and_1 (C_out, B, A);
endmodule

module full_adder (
  input  A,
  input  B,
  input  C_in,
  output S,
  output C_out
);

  wire and_1_out, and_2_out, xor_1_out;

  xor xor_1 (xor_1_out, B, A);
  and and_1 (and_1_out, xor_1_out, C_in);
  and and_2 (and_2_out, B, A);
  xor xor_2 (S, xor_1_out, C_in);
  or or_1 (C_out, and_1_out, and_2_out);
endmodule
