// Logisim project cast.circ as structural Verilog: 3 circuits, main circuit sign2two4
module sign2two4 (
  input  [3:0] A,
  output [3:0] out_2
);

  wire full_adder_1_c_out, full_adder_2_c_out, full_adder_3_c_out, xor_1_out, xor_2_out, xor_3_out;

  xor xor_1 (xor_1_out, A[0], A[3]);
  xor xor_2 (xor_2_out, A[1], A[3]);
  xor xor_3 (xor_3_out, A[2], A[3]);
  full_adder full_adder_1 (.B(1'b0), .C_in(A[3]), .A(xor_1_out), .S(out_2[0]), .C_out(full_adder_1_c_out));
  full_adder full_adder_2 (
    .B(1'b0), .C_in(full_adder_1_c_out), .A(xor_2_out), .S(out_2[1]), .C_out(full_adder_2_c_out));
  full_adder full_adder_3 (
    .B(1'b0), .C_in(full_adder_2_c_out), .A(xor_3_out), .S(out_2[2]), .C_out(full_adder_3_c_out));
  // NoConnect on full_adder_3_c_out

  assign out_2[3] = A[3];
endmodule

module two2sign4 (
  input  [3:0] A,
  output [3:0] out_2
);

  wire full_adder_1_c_out, full_adder_1_s, full_adder_2_c_out, full_adder_2_s, full_adder_3_c_out,
       full_adder_3_s;

  // NoConnect on full_adder_3_c_out
  full_adder full_adder_1 (.B(A[3]), .C_in(1'b0), .A(A[0]), .S(full_adder_1_s), .C_out(full_adder_1_c_out));
  full_adder full_adder_2 (
    .B(A[3]), .C_in(full_adder_1_c_out), .A(A[1]), .S(full_adder_2_s), .C_out(full_adder_2_c_out));
  full_adder full_adder_3 (
    .B(A[3]), .C_in(full_adder_2_c_out), .A(A[2]), .S(full_adder_3_s), .C_out(full_adder_3_c_out));
  xor xor_1 (out_2[0], full_adder_1_s, A[3]);
  xor xor_2 (out_2[1], full_adder_2_s, A[3]);
  xor xor_3 (out_2[2], full_adder_3_s, A[3]);

  assign out_2[3] = A[3];
endmodule

module trunc_8_to_4 (
  input  [7:0] A,
  output [3:0] S
);

  // NoConnect on A[0]
  // NoConnect on A[1]
  // NoConnect on A[2]
  // NoConnect on A[3]

  assign S = A[7:4];
endmodule
