// Logisim project cast_simple.circ as structural Verilog
module cast_demo (
  input  [3:0] in_1,
  output [3:0] S
);

  wire sum4_1_c_out;
  wire [3:0] bnot4_1_s;

  bnot4 bnot4_1 (.A({1'b0, in_1[2:0]}), .I(in_1[3]), .S(bnot4_1_s));
  sum4 sum4_1 (.B(4'b0001), .A(bnot4_1_s), .C_out(sum4_1_c_out), .S(S));
  // NoConnect on sum4_1_c_out
endmodule

module sign2two4 (
  input  [3:0] in_1,
  output [3:0] S
);

  wire sum4_1_c_out;
  wire [3:0] bnot4_1_s;

  bnot4 bnot4_1 (.A({1'b0, in_1[2:0]}), .I(in_1[3]), .S(bnot4_1_s));
  sum4 sum4_1 (.B(4'b0001), .A(bnot4_1_s), .C_out(sum4_1_c_out), .S(S));
  // NoConnect on sum4_1_c_out
endmodule
