// Logisim project extend.circ as structural Verilog: 1 circuit, main circuit ext_7_to_8_sign
module ext_7_to_8_sign (
  input  [6:0] A,
  output [7:0] S
);


  assign S = {A[6], 1'b0, A[5:0]};
endmodule
