// Logisim project inv.circ as structural Verilog: 3 circuits, main circuit inv_demo
module inv_demo (
  input  [3:0] in_1,
  output [3:0] out_2
);

  wire dipswitch_1_sw1;

  Hex_Digit_Display hex_digit_display_1 (.value(in_1));  // open: dp
  DipSwitch dipswitch_1 (.sw1(dipswitch_1_sw1));  // open: sw2, sw3, sw4, sw5, sw6, sw7, sw8
  Hex_Digit_Display hex_digit_display_2 (.value(out_2));  // open: dp
  bnot4 bnot4_1 (.A(in_1), .I(dipswitch_1_sw1), .S(out_2));
endmodule

module bnot4 (
  input  [3:0] A,
  input  I,
  output [3:0] S
);

  xor xor_1 (S[0], A[0], I);
  xor xor_2 (S[1], A[1], I);
  xor xor_3 (S[2], A[2], I);
  xor xor_4 (S[3], A[3], I);
endmodule

module bnot8 (
  input  [7:0] A,
  input  I,
  output [7:0] S
);

  xor xor_1 (S[0], A[0], I);
  xor xor_2 (S[1], A[1], I);
  xor xor_3 (S[2], A[2], I);
  xor xor_4 (S[3], A[3], I);
  xor xor_5 (S[4], A[4], I);
  xor xor_6 (S[5], A[5], I);
  xor xor_7 (S[6], A[6], I);
  xor xor_8 (S[7], A[7], I);
endmodule
