// Logisim project ReLu.circ as structural Verilog: 1 circuit, main circuit main
module main (
  input  [3:0] in_1,
  output [3:0] out_2
);

  wire not_1_out;

  not not_1 (not_1_out, in_1[3]);
  and and_1 (out_2[0], not_1_out, in_1[0]);
  and and_2 (out_2[1], not_1_out, in_1[1]);
  and and_3 (out_2[2], not_1_out, in_1[2]);

  assign out_2[3] = 1'b0;
endmodule
