// Logisim project display_hex.circ as structural Verilog: 1 circuit, main circuit main
module main (
  input  A,
  input  B,
  input  C,
  input  D
);

  wire AB_out, ABDn_out, ABn_out, ABnCn_out, AC_out, ACDn_out, ACnD_out, ACnDn_out, AD_out, ADn_out, AnB_out,
       AnBCn_out, AnBD_out, AnBn_out, AnBnDn_out, AnC_out, AnCD_out, AnCDn_out, AnCnDn_out, BC_out, BCnD_out,
       BDn_out, BnC_out, BnCD_out, BnCn_out, BnD_out, BnDn_out, CDn_out, CnD_out, CnDn_out, not_1_out,
       not_2_out, not_3_out, not_4_out, or_1_out, or_2_out, or_3_out, or_4_out, or_5_out, or_6_out, or_7_out;

  not not_1 (not_1_out, A);
  not not_2 (not_2_out, B);
  not not_3 (not_3_out, C);
  not not_4 (not_4_out, D);
  and BnDn (BnDn_out, not_4_out, not_2_out);
  and ABnCn (ABnCn_out, not_3_out, not_2_out, A);
  and ADn (ADn_out, A, not_4_out);
  and AnBD (AnBD_out, D, B, not_1_out);
  and AnC (AnC_out, C, not_1_out);
  and BC (BC_out, C, B);
  and AnBn (AnBn_out, not_2_out, not_1_out);
  and BnCn (BnCn_out, not_3_out, not_2_out);
  and AnCnDn (AnCnDn_out, not_4_out, not_3_out, not_1_out);
  and AnCD (AnCD_out, D, C, not_1_out);
  and ACDn (ACDn_out, not_4_out, C, A);
  and ACnD (ACnD_out, D, not_3_out, A);
  and AnB (AnB_out, B, not_1_out);
  and CnD (CnD_out, D, not_3_out);
  and BnD (BnD_out, D, not_2_out);
  and ABn (ABn_out, not_2_out, A);
  and BCnD (BCnD_out, D, not_3_out, B);
  and ABDn (ABDn_out, not_4_out, B, A);
  and BnCD (BnCD_out, D, C, not_2_out);
  and ACnDn (ACnDn_out, not_4_out, not_3_out, A);
  and AnCDn (AnCDn_out, not_4_out, C, not_1_out);
  and AnBnDn (AnBnDn_out, not_4_out, not_2_out, not_1_out);
  and AB (AB_out, B, A);
  and CDn (CDn_out, not_4_out, C);
  and AC (AC_out, C, A);
  and CnDn (CnDn_out, not_4_out, not_3_out);
  and AnBCn (AnBCn_out, not_3_out, B, not_1_out);
  and BDn (BDn_out, not_4_out, B);
  and AD (AD_out, D, A);
  and BnC (BnC_out, C, not_2_out);
  or or_1 (or_1_out, BnDn_out, ABnCn_out, ADn_out, AnBD_out, AnC_out, BC_out);
  or or_2 (or_2_out, AnBn_out, BnCn_out, AnCnDn_out, AnCD_out, ACDn_out, ACnD_out);
  or or_3 (or_3_out, BnCn_out, AnB_out, CnD_out, BnD_out, ABn_out);
  or or_4 (or_4_out, CnDn_out, ABn_out, AnBCn_out, BDn_out, AC_out);
  or or_5 (or_5_out, BCnD_out, ABDn_out, BnCD_out, ACnDn_out, AnCDn_out, AnBnDn_out);
  or or_6 (or_6_out, BnDn_out, AB_out, CDn_out, AC_out);
  or or_7 (or_7_out, CDn_out, AnBCn_out, ABn_out, AD_out, BnC_out);
  _7_Segment_Display u_7_segment_display_1 (
    .g(or_7_out), .f(or_4_out), .a(or_1_out), .b(or_2_out), .e(or_6_out), .d(or_5_out), .c(or_3_out));  // open: dp
endmodule
