// Logisim project ReLu.circ as structural Verilog: 1 circuit, main circuit main
module main (
  input  [3:0] in_1,
  output [3:0] out_2
);

  wire not_1_out, not_2_out, not_3_out, not_4_out;

  not not_1 (not_1_out, in_1[3]);
  not not_2 (not_2_out, in_1[0]);
  not not_3 (not_3_out, in_1[2]);
  not not_4 (not_4_out, in_1[1]);
  and and_1 (out_2[0], not_1_out, in_1[0]);
  and and_2 (out_2[1], not_1_out, in_1[1]);
  and and_3 (out_2[2], not_1_out, in_1[2]);
  and and_4 (out_2[3], not_2_out, not_3_out, in_1[3], not_4_out);
endmodule
