// Logisim project mul.circ as structural Verilog: 2 circuits, main circuit mul4_sign
module mul4_sign (
  input  [3:0] A,
  input  [3:0] B,
  output [6:0] S
);

  wire full_mul_1_c_out, full_mul_2_c_out, full_mul_2_s, full_mul_3_c_out, full_mul_3_s, full_mul_4_c_out,
       full_mul_5_c_out, full_mul_5_s, full_mul_6_c_out, full_mul_6_s, full_mul_7_c_out, full_mul_8_c_out;

  full_mul full_mul_1 (.B(B[0]), .P(1'b0), .C_in(1'b0), .A(A[0]), .S(S[0]), .C_out(full_mul_1_c_out));
  // NoConnect on A[3]
  full_mul full_mul_2 (
    .B(B[0]), .P(1'b0), .C_in(full_mul_1_c_out), .A(A[1]), .S(full_mul_2_s), .C_out(full_mul_2_c_out));
  full_mul full_mul_3 (
    .B(B[0]), .P(1'b0), .C_in(full_mul_2_c_out), .A(A[2]), .S(full_mul_3_s), .C_out(full_mul_3_c_out));
  xor xor_1 (S[6], A[3], B[3]);
  full_mul full_mul_4 (.B(B[1]), .P(full_mul_2_s), .C_in(1'b0), .A(A[0]), .S(S[1]), .C_out(full_mul_4_c_out));
  // NoConnect on A[3]
  full_mul full_mul_5 (
    .B(B[1]), .P(full_mul_3_s), .C_in(full_mul_4_c_out), .A(A[1]), .S(full_mul_5_s), .C_out(full_mul_5_c_out));
  full_mul full_mul_6 (
    .B(B[1]), .P(full_mul_3_c_out), .C_in(full_mul_5_c_out), .A(A[2]), .S(full_mul_6_s),
    .C_out(full_mul_6_c_out));
  full_mul full_mul_7 (.B(B[2]), .P(full_mul_5_s), .C_in(1'b0), .A(A[0]), .S(S[2]), .C_out(full_mul_7_c_out));
  full_mul full_mul_8 (
    .B(B[2]), .P(full_mul_6_s), .C_in(full_mul_7_c_out), .A(A[1]), .S(S[3]), .C_out(full_mul_8_c_out));
  full_mul full_mul_9 (.B(B[2]), .P(full_mul_6_c_out), .C_in(full_mul_8_c_out), .A(A[2]), .S(S[4]), .C_out(S[5]));

  // Other names for the same wires on the sheet: B_tunel_1 = B[1]; B_tunel_2 = B[2]

  // Notes on the sheet:
  //   Multiplicator of 4 bits with sign
endmodule

module mul4 (
  input  [3:0] A,
  input  [3:0] B,
  output [7:0] S
);

  wire full_mul_1_c_out, full_mul_2_c_out, full_mul_2_s, full_mul_3_c_out, full_mul_3_s, full_mul_4_c_out,
       full_mul_4_s, full_mul_5_c_out, full_mul_6_c_out, full_mul_6_s, full_mul_7_c_out, full_mul_7_s,
       full_mul_8_c_out, full_mul_8_s, full_mul_9_c_out, full_mul_10_c_out, full_mul_10_s, full_mul_11_c_out,
       full_mul_11_s, full_mul_12_c_out, full_mul_12_s, full_mul_13_c_out, full_mul_14_c_out,
       full_mul_15_c_out;

  full_mul full_mul_1 (.B(B[0]), .P(1'b0), .C_in(1'b0), .A(A[0]), .S(S[0]), .C_out(full_mul_1_c_out));
  full_mul full_mul_2 (
    .B(B[0]), .P(1'b0), .C_in(full_mul_1_c_out), .A(A[1]), .S(full_mul_2_s), .C_out(full_mul_2_c_out));
  full_mul full_mul_3 (
    .B(B[0]), .P(1'b0), .C_in(full_mul_2_c_out), .A(A[2]), .S(full_mul_3_s), .C_out(full_mul_3_c_out));
  full_mul full_mul_4 (
    .B(B[0]), .P(1'b0), .C_in(full_mul_3_c_out), .A(A[3]), .S(full_mul_4_s), .C_out(full_mul_4_c_out));
  full_mul full_mul_5 (.B(B[1]), .P(full_mul_2_s), .C_in(1'b0), .A(A[0]), .S(S[1]), .C_out(full_mul_5_c_out));
  full_mul full_mul_6 (
    .B(B[1]), .P(full_mul_3_s), .C_in(full_mul_5_c_out), .A(A[1]), .S(full_mul_6_s), .C_out(full_mul_6_c_out));
  full_mul full_mul_7 (
    .B(B[1]), .P(full_mul_4_s), .C_in(full_mul_6_c_out), .A(A[2]), .S(full_mul_7_s), .C_out(full_mul_7_c_out));
  full_mul full_mul_8 (
    .B(B[1]), .P(full_mul_4_c_out), .C_in(full_mul_7_c_out), .A(A[3]), .S(full_mul_8_s),
    .C_out(full_mul_8_c_out));
  full_mul full_mul_9 (.B(B[2]), .P(full_mul_6_s), .C_in(1'b0), .A(A[0]), .S(S[2]), .C_out(full_mul_9_c_out));
  full_mul full_mul_10 (
    .B(B[2]), .P(full_mul_7_s), .C_in(full_mul_9_c_out), .A(A[1]), .S(full_mul_10_s),
    .C_out(full_mul_10_c_out));
  full_mul full_mul_11 (
    .B(B[2]), .P(full_mul_8_s), .C_in(full_mul_10_c_out), .A(A[2]), .S(full_mul_11_s),
    .C_out(full_mul_11_c_out));
  full_mul full_mul_12 (
    .B(B[2]), .P(full_mul_8_c_out), .C_in(full_mul_11_c_out), .A(A[3]), .S(full_mul_12_s),
    .C_out(full_mul_12_c_out));
  full_mul full_mul_13 (.B(B[3]), .P(full_mul_10_s), .C_in(1'b0), .A(A[0]), .S(S[3]), .C_out(full_mul_13_c_out));
  full_mul full_mul_14 (
    .B(B[3]), .P(full_mul_11_s), .C_in(full_mul_13_c_out), .A(A[1]), .S(S[4]), .C_out(full_mul_14_c_out));
  full_mul full_mul_15 (
    .B(B[3]), .P(full_mul_12_s), .C_in(full_mul_14_c_out), .A(A[2]), .S(S[5]), .C_out(full_mul_15_c_out));
  full_mul full_mul_16 (.B(B[3]), .P(full_mul_12_c_out), .C_in(full_mul_15_c_out), .A(A[3]), .S(S[6]), .C_out(S[7]));

  // Other names for the same wires on the sheet: B_tunel_1 = B[1]; B_tunel_2 = B[2]; B_tunel_3 = B[3]
endmodule
