// Logisim project sigmoid.circ as structural Verilog: 1 circuit, main circuit main
module main (
  input  [3:0] I,
  output [3:0] O
);

  wire and_3_out, and_4_out, and_5_out, and_6_out, and_7_out, not_1_out, not_2_out, not_3_out, not_4_out,
       not_5_out, not_6_out, or_1_out;

  not not_1 (not_1_out, I[0]);
  not not_2 (not_2_out, I[1]);
  not not_3 (not_3_out, I[2]);
  not not_4 (not_4_out, I[2]);
  not not_5 (not_5_out, I[1]);
  not not_6 (not_6_out, I[0]);
  and and_1 (O[3], I[3], not_1_out, not_2_out, not_3_out);
  not not_7 (O[2], I[3]);
  or or_1 (or_1_out, I[0], I[1], I[2]);
  and and_2 (O[1], or_1_out, I[3]);
  and and_3 (and_3_out, O[2], I[2], I[1]);
  and and_4 (and_4_out, I[3], not_4_out, I[1]);
  and and_5 (and_5_out, I[3], I[2], not_5_out, not_6_out);
  and and_6 (and_6_out, O[2], I[2], not_5_out, I[0]);
  and and_7 (and_7_out, I[3], not_4_out, not_5_out, I[0]);
  or or_2 (O[0], and_3_out, and_4_out, and_5_out, and_6_out, and_7_out);
endmodule
