// Logisim project sum.circ as structural Verilog: 2 circuits, main circuit sum4
module sum4 (
  input  [3:0] A,
  input  [3:0] B,
  output [3:0] S,
  output C_out
);

  wire full_adder_1_c_out, full_adder_2_c_out, full_adder_3_c_out;

  full_adder full_adder_1 (.B(B[0]), .C_in(1'b0), .A(A[0]), .S(S[0]), .C_out(full_adder_1_c_out));
  full_adder full_adder_2 (.B(B[1]), .C_in(full_adder_1_c_out), .A(A[1]), .S(S[1]), .C_out(full_adder_2_c_out));
  full_adder full_adder_3 (.B(B[2]), .C_in(full_adder_2_c_out), .A(A[2]), .S(S[2]), .C_out(full_adder_3_c_out));
  full_adder full_adder_4 (.B(B[3]), .C_in(full_adder_3_c_out), .A(A[3]), .S(S[3]), .C_out(C_out));
endmodule

module sum8 (
  input  [7:0] A,
  input  [7:0] B,
  output [7:0] S,
  output C_out
);

  wire full_adder_1_c_out, full_adder_2_c_out, full_adder_3_c_out, full_adder_4_c_out, full_adder_5_c_out,
       full_adder_6_c_out, full_adder_7_c_out;

  full_adder full_adder_1 (.B(B[0]), .C_in(1'b0), .A(A[0]), .S(S[0]), .C_out(full_adder_1_c_out));
  full_adder full_adder_2 (.B(B[1]), .C_in(full_adder_1_c_out), .A(A[1]), .S(S[1]), .C_out(full_adder_2_c_out));
  full_adder full_adder_3 (.B(B[2]), .C_in(full_adder_2_c_out), .A(A[2]), .S(S[2]), .C_out(full_adder_3_c_out));
  full_adder full_adder_4 (.B(B[3]), .C_in(full_adder_3_c_out), .A(A[3]), .S(S[3]), .C_out(full_adder_4_c_out));
  full_adder full_adder_5 (.B(B[4]), .C_in(full_adder_4_c_out), .A(A[4]), .S(S[4]), .C_out(full_adder_5_c_out));
  full_adder full_adder_6 (.B(B[5]), .C_in(full_adder_5_c_out), .A(A[5]), .S(S[5]), .C_out(full_adder_6_c_out));
  full_adder full_adder_7 (.B(B[6]), .C_in(full_adder_6_c_out), .A(A[6]), .S(S[6]), .C_out(full_adder_7_c_out));
  full_adder full_adder_8 (.B(B[7]), .C_in(full_adder_7_c_out), .A(A[7]), .S(S[7]), .C_out(C_out));
endmodule
