// Logisim project sum_c1.circ as structural Verilog: 5 circuits, main circuit main
module main (
  input  [3:0] i1,
  input  [3:0] of_output,
  input  [3:0] uf_output,
  input  [3:0] i0,
  output [3:0] out_5
);

  wire not_1_out, not_2_out, sum_1_c_out0, sum_1_c_out1, sum_2_c_out0, sum_2_c_out1, sum_3_c_out0,
       sum_3_c_out1, sum_4_c_out0, xor_1_out, xor_2_out, xor_3_out, xor_4_out, xor_5_out, xor_6_out;
  wire [1:0] and_2_out;
  wire [3:0] sum_1_s;

  xor xor_1 (xor_1_out, i1[0], i1[3]);
  xor xor_2 (xor_2_out, i1[1], i1[3]);
  xor xor_3 (xor_3_out, i1[2], i1[3]);
  xor xor_4 (xor_4_out, i0[0], i0[3]);
  xor xor_5 (xor_5_out, i0[1], i0[3]);
  xor xor_6 (xor_6_out, i0[2], i0[3]);
  sum sum_1 (
    .C0(i1[3]), .C1(i0[3]), .A(xor_1_out), .B(xor_4_out), .S(sum_1_s[0]), .C_out1(sum_1_c_out1),
    .C_out0(sum_1_c_out0));
  sum sum_2 (
    .C0(sum_1_c_out1), .C1(sum_1_c_out0), .A(xor_2_out), .B(xor_5_out), .S(sum_1_s[1]),
    .C_out1(sum_2_c_out1), .C_out0(sum_2_c_out0));
  sum sum_3 (
    .C0(sum_2_c_out1), .C1(sum_2_c_out0), .A(xor_3_out), .B(xor_6_out), .S(sum_1_s[2]),
    .C_out1(sum_3_c_out1), .C_out0(sum_3_c_out0));
  sum sum_4 (
    .C0(sum_3_c_out1), .C1(sum_3_c_out0), .A(i1[3]), .B(i0[3]), .S(sum_1_s[3]), .C_out0(sum_4_c_out0));  // open: C_out1
  and and_1 (and_2_out[1], sum_1_s[3], sum_4_c_out0);
  and and_2 (and_2_out[0], sum_1_s[3], not_1_out, not_2_out);
  not not_1 (not_1_out, i1[3]);
  not not_2 (not_2_out, i0[3]);
  Multiplexer #(.select(2), .width(4)) multiplexer_1 (
    .in0(sum_1_s), .in1(of_output), .in2(uf_output), .out(out_5), .sel(and_2_out));  // open: in3
endmodule

module sum (
  input  C0,
  input  C1,
  input  A,
  input  B,
  output S,
  output C_out1,
  output C_out0
);

  wire and_1_out, and_2_out, xor_1_out, xor_2_out;

  xor xor_1 (xor_1_out, C0, C1);
  xor xor_2 (xor_2_out, B, A);
  and and_1 (and_1_out, xor_2_out, xor_1_out);
  and and_2 (and_2_out, B, A);
  and and_3 (C_out1, C1, C0);
  xor xor_3 (S, xor_2_out, xor_1_out);
  or or_1 (C_out0, and_1_out, and_2_out);
endmodule

module anom_flow_detection (
  input  last_cout0,
  input  output_sinal,
  input  sinal0,
  input  sinal1,
  output underflow,
  output overflow
);

  wire not_1_out, not_2_out;

  and and_1 (underflow, last_cout0, output_sinal);
  and and_2 (overflow, output_sinal, not_1_out, not_2_out);
  not not_1 (not_1_out, sinal0);
  not not_2 (not_2_out, sinal1);
endmodule

module modular (
  input  [3:0] i1,
  input  [3:0] i0,
  input  Cin1,
  input  Cin0,
  output [3:0] output_c2,
  output Cout1,
  output Cout0
);

  wire sum_1_c_out0, sum_1_c_out1, sum_2_c_out0, sum_2_c_out1, sum_3_c_out0, sum_3_c_out1;

  sum sum_1 (
    .C0(Cin0), .C1(Cin1), .A(i1[0]), .B(i0[0]), .S(output_c2[0]), .C_out1(sum_1_c_out1), .C_out0(sum_1_c_out0));
  sum sum_2 (
    .C0(sum_1_c_out1), .C1(sum_1_c_out0), .A(i1[1]), .B(i0[1]), .S(output_c2[1]), .C_out1(sum_2_c_out1),
    .C_out0(sum_2_c_out0));
  sum sum_3 (
    .C0(sum_2_c_out1), .C1(sum_2_c_out0), .A(i1[2]), .B(i0[2]), .S(output_c2[2]), .C_out1(sum_3_c_out1),
    .C_out0(sum_3_c_out0));
  sum sum_4 (
    .C0(sum_3_c_out1), .C1(sum_3_c_out0), .A(i1[3]), .B(i0[3]), .S(output_c2[3]), .C_out1(Cout1),
    .C_out0(Cout0));
endmodule

module main_8bit (
  input  [7:0] i1,
  input  [7:0] i0,
  output [7:0] regular_output,
  output [7:0] selected_output
);

  wire modular_1_cout0, modular_2_cout0, modular_2_cout1;
  wire [1:0] anom_flow_detection_1_overflow;
  wire [2:0] xor_5_out, xor_12_out;
  wire [3:0] xor_1_out, xor_8_out;

  xor xor_1 (xor_1_out[0], i1[0], i1[7]);
  xor xor_2 (xor_1_out[1], i1[1], i1[7]);
  xor xor_3 (xor_1_out[2], i1[2], i1[7]);
  xor xor_4 (xor_1_out[3], i1[3], i1[7]);
  xor xor_5 (xor_5_out[0], i1[4], i1[7]);
  xor xor_6 (xor_5_out[1], i1[5], i1[7]);
  xor xor_7 (xor_5_out[2], i1[6], i1[7]);
  xor xor_8 (xor_8_out[0], i0[0], i0[7]);
  xor xor_9 (xor_8_out[1], i0[1], i0[7]);
  xor xor_10 (xor_8_out[2], i0[2], i0[7]);
  xor xor_11 (xor_8_out[3], i0[3], i0[7]);
  xor xor_12 (xor_12_out[0], i0[4], i0[7]);
  xor xor_13 (xor_12_out[1], i0[5], i0[7]);
  xor xor_14 (xor_12_out[2], i0[6], i0[7]);
  modular modular_1 (
    .i1({i1[7], xor_5_out}), .i0({i0[7], xor_12_out}), .Cin1(modular_2_cout1), .Cin0(modular_2_cout0),
    .output_c2(regular_output[7:4]), .Cout0(modular_1_cout0));  // open: Cout1
  modular modular_2 (
    .i1(xor_1_out), .i0(xor_8_out), .Cin1(i1[7]), .Cin0(i0[7]), .output_c2(regular_output[3:0]),
    .Cout1(modular_2_cout1), .Cout0(modular_2_cout0));
  anom_flow_detection anom_flow_detection_1 (
    .last_cout0(modular_1_cout0), .output_sinal(regular_output[7]), .sinal0(i0[7]), .sinal1(i1[7]),
    .underflow(anom_flow_detection_1_overflow[1]), .overflow(anom_flow_detection_1_overflow[0]));
  Multiplexer #(.select(2), .width(8)) multiplexer_1 (
    .in0(regular_output), .in1(8'h7f), .in2(8'h81), .out(selected_output),
    .sel(anom_flow_detection_1_overflow));  // open: in3
endmodule
