// Logisim project tanH.circ as structural Verilog: 1 circuit, main circuit main
module main (
  input  [3:0] I,
  output [3:0] O
);

  wire and_2_out, and_3_out, not_1_out, not_2_out;

  not not_1 (not_1_out, I[2]);
  not not_2 (not_2_out, I[2]);
  and and_1 (O[1], not_2_out, I[1]);
  and and_2 (and_2_out, I[2], I[1]);
  and and_3 (and_3_out, not_1_out, I[0]);
  or or_1 (O[0], and_2_out, and_3_out);

  assign O[3:2] = I[3:2];
endmodule
