// Logisim project counter.circ as structural Verilog
module fifo_4b_3n (
  input  [3:0] A,
  input  enable,
  input  clk,
  input  clear,
  output [3:0] S
);

  wire [3:0] reg4_1_q, reg4_2_q, reg4_3_q;

  reg4 reg4_1 (.clear(clear), .enable(enable), .clk(clk), .D(A), .Q(reg4_1_q));
  reg4 reg4_2 (.clear(clear), .enable(enable), .clk(clk), .D(reg4_1_q), .Q(reg4_2_q));
  reg4 reg4_3 (.clear(clear), .enable(enable), .clk(clk), .D(reg4_2_q), .Q(reg4_3_q));
  reg4 reg4_4 (.clear(clear), .enable(enable), .clk(clk), .D(reg4_3_q), .Q(S));
endmodule
