// Logisim project registers.circ as structural Verilog: 3 circuits, main circuit reg4
module reg4 (
  input  [3:0] D,
  input  clk,
  input  enable,
  input  clear,
  output [3:0] Q
);

  wire and_1_out, d_ff_1_qn, d_ff_2_qn, d_ff_3_qn, d_ff_4_qn;

  and and_1 (and_1_out, enable, clk);
  D_Flip_Flop d_ff_1 (.D(D[0]), .clk(and_1_out), .Q(Q[0]), .Qn(d_ff_1_qn), .preset(1'b0), .reset(clear));
  D_Flip_Flop d_ff_2 (.D(D[1]), .clk(and_1_out), .Q(Q[1]), .Qn(d_ff_2_qn), .preset(1'b0), .reset(clear));
  D_Flip_Flop d_ff_3 (.D(D[2]), .clk(and_1_out), .Q(Q[2]), .Qn(d_ff_3_qn), .preset(1'b0), .reset(clear));
  D_Flip_Flop d_ff_4 (.D(D[3]), .clk(and_1_out), .Q(Q[3]), .Qn(d_ff_4_qn), .preset(1'b0), .reset(clear));
  // NoConnect on d_ff_1_qn
  // NoConnect on d_ff_2_qn
  // NoConnect on d_ff_3_qn
  // NoConnect on d_ff_4_qn
endmodule

module reg8 (
  input  [7:0] D,
  input  clk,
  input  enable,
  input  clear,
  output [7:0] Q
);

  wire and_1_out, d_ff_1_qn, d_ff_2_qn, d_ff_3_qn, d_ff_4_qn, d_ff_5_qn, d_ff_6_qn, d_ff_7_qn, d_ff_8_qn;

  and and_1 (and_1_out, enable, clk);
  D_Flip_Flop d_ff_1 (.D(D[0]), .clk(and_1_out), .Q(Q[0]), .Qn(d_ff_1_qn), .preset(1'b0), .reset(clear));
  D_Flip_Flop d_ff_2 (.D(D[1]), .clk(and_1_out), .Q(Q[1]), .Qn(d_ff_2_qn), .preset(1'b0), .reset(clear));
  D_Flip_Flop d_ff_3 (.D(D[2]), .clk(and_1_out), .Q(Q[2]), .Qn(d_ff_3_qn), .preset(1'b0), .reset(clear));
  D_Flip_Flop d_ff_4 (.D(D[3]), .clk(and_1_out), .Q(Q[3]), .Qn(d_ff_4_qn), .preset(1'b0), .reset(clear));
  D_Flip_Flop d_ff_5 (.D(D[4]), .clk(and_1_out), .Q(Q[4]), .Qn(d_ff_5_qn), .preset(1'b0), .reset(clear));
  D_Flip_Flop d_ff_6 (.D(D[5]), .clk(and_1_out), .Q(Q[5]), .Qn(d_ff_6_qn), .preset(1'b0), .reset(clear));
  D_Flip_Flop d_ff_7 (.D(D[6]), .clk(and_1_out), .Q(Q[6]), .Qn(d_ff_7_qn), .preset(1'b0), .reset(clear));
  D_Flip_Flop d_ff_8 (.D(D[7]), .clk(and_1_out), .Q(Q[7]), .Qn(d_ff_8_qn), .preset(1'b0), .reset(clear));
  // NoConnect on d_ff_1_qn
  // NoConnect on d_ff_2_qn
  // NoConnect on d_ff_3_qn
  // NoConnect on d_ff_4_qn
  // NoConnect on d_ff_5_qn
  // NoConnect on d_ff_6_qn
  // NoConnect on d_ff_7_qn
  // NoConnect on d_ff_8_qn

  // Notes on the sheet:
  //   clear
  //   clk
endmodule

module reg2 (
  input  [1:0] D,
  input  clk,
  input  enable,
  input  clear,
  output [1:0] Q
);

  wire and_1_out, d_ff_1_qn, d_ff_2_qn;

  and and_1 (and_1_out, enable, clk);
  D_Flip_Flop d_ff_1 (.D(D[0]), .clk(and_1_out), .Q(Q[0]), .Qn(d_ff_1_qn), .preset(1'b0), .reset(clear));
  D_Flip_Flop d_ff_2 (.D(D[1]), .clk(and_1_out), .Q(Q[1]), .Qn(d_ff_2_qn), .preset(1'b0), .reset(clear));
  // NoConnect on d_ff_1_qn
  // NoConnect on d_ff_2_qn
endmodule
