// Logisim project seq.circ as structural Verilog
module fifo_4b_3n (
);

  // reg4 reg4_1: pin names not known
  // reg4 reg4_2: pin names not known
  // reg4 reg4_3: pin names not known
  // reg4 reg4_4: pin names not known
endmodule
