// Logisim project pe.circ as structural Verilog: 1 circuit, main circuit pe4
module pe4 (
  input  [3:0] N,
  input  answer,
  input  [3:0] M,
  input  clk,
  input  clear,
  input  enable,
  output [3:0] Q,
  output [7:0] S,
  output [3:0] P
);

  wire sum8_1_c_out;
  wire [3:0] multiplexer_1_out, trunc_8_to_4_1_s;
  wire [6:0] mul4_sign_1_s;
  wire [7:0] ext_7_to_8_sign_1_s, sum8_1_s;

  reg4 N_TEMP (.clear(clear), .enable(1'b1), .clk(clk), .D(N), .Q(P));
  mul4_sign mul4_sign_1 (.B(M), .A(N), .S(mul4_sign_1_s));
  ext_7_to_8_sign ext_7_to_8_sign_1 (.A(mul4_sign_1_s), .S(ext_7_to_8_sign_1_s));
  Multiplexer #(.width(4)) multiplexer_1 (.in0(M), .in1(trunc_8_to_4_1_s), .out(multiplexer_1_out), .sel(answer));
  sum8 sum8_1 (.B(S), .A(ext_7_to_8_sign_1_s), .C_out(sum8_1_c_out), .S(sum8_1_s));
  // NoConnect on sum8_1_c_out
  reg4 M_TEMP (.clear(clear), .enable(1'b1), .clk(clk), .D(multiplexer_1_out), .Q(Q));
  trunc_8_to_4 trunc_8_to_4_1 (.A(S), .S(trunc_8_to_4_1_s));
  reg8 ACC (.enable(enable), .clk(clk), .D(sum8_1_s), .clear(clear), .Q(S));
endmodule
