// Logisim project arrays.circ as structural Verilog: 2 circuits, main circuit skeleton_3x3_4b
module skeleton_3x3_4b (
  input  [3:0] N_column_1,
  input  [3:0] N_column_2,
  input  [3:0] N_column_3,
  input  [3:0] M_line_1,
  input  [3:0] M_line_2,
  input  [3:0] M_line_3,
  input  clear,
  input  enable,
  input  answer,
  input  clk,
  output [3:0] S1,
  output [3:0] S2,
  output [3:0] S3
);

  wire [3:0] pe4_1_p, pe4_1_q, pe4_2_p, pe4_2_q, pe4_3_q, pe4_4_p, pe4_4_q, pe4_5_p, pe4_5_q, pe4_6_q,
       pe4_7_p, pe4_8_p;
  wire [7:0] pe4_1_s;

  pe4 pe4_1 (
    .M(M_line_1), .clk(clk), .clear(clear), .N(N_column_1), .answer(answer), .enable(enable), .P(pe4_1_p),
    .S(pe4_1_s), .Q(pe4_1_q));
  pe4 pe4_2 (
    .M(M_line_2), .clk(clk), .clear(clear), .N(pe4_1_p), .answer(answer), .enable(enable), .P(pe4_2_p),
    .Q(pe4_2_q));  // open: S
  pe4 pe4_3 (
    .M(M_line_3), .clk(clk), .clear(clear), .N(pe4_2_p), .answer(answer), .enable(enable), .Q(pe4_3_q));  // open: P, S
  pe4 pe4_4 (
    .M(pe4_1_q), .clk(clk), .clear(clear), .N(N_column_2), .answer(answer), .enable(enable), .P(pe4_4_p),
    .Q(pe4_4_q));  // open: S
  pe4 pe4_5 (
    .M(pe4_2_q), .clk(clk), .clear(clear), .N(pe4_4_p), .answer(answer), .enable(enable), .P(pe4_5_p),
    .Q(pe4_5_q));  // open: S
  pe4 pe4_6 (
    .M(pe4_3_q), .clk(clk), .clear(clear), .N(pe4_5_p), .answer(answer), .enable(enable), .Q(pe4_6_q));  // open: P, S
  pe4 pe4_7 (
    .M(pe4_4_q), .clk(clk), .clear(clear), .N(N_column_3), .answer(answer), .enable(enable), .P(pe4_7_p),
    .Q(S1));  // open: S
  pe4 pe4_8 (
    .M(pe4_5_q), .clk(clk), .clear(clear), .N(pe4_7_p), .answer(answer), .enable(enable), .P(pe4_8_p), .Q(S2));  // open: S
  pe4 pe4_9 (
    .M(pe4_6_q), .clk(clk), .clear(clear), .N(pe4_8_p), .answer(answer), .enable(enable), .Q(S3));  // open: P, S
endmodule

module arr_3x3_4b (
  input  in_1,
  input  in_2,
  input  in_3,
  input  in_4
);

  wire [3:0] undriven, undriven_2, undriven_3, undriven_4, undriven_5, undriven_6;

  // fifo_4b_3n fifo_4b_3n_1: pin names not known
  // fifo_4b_3n fifo_4b_3n_2: pin names not known
  // fifo_4b_3n fifo_4b_3n_3: pin names not known
  // fifo_4b_3n fifo_4b_3n_4: pin names not known
  // fifo_4b_3n fifo_4b_3n_5: pin names not known
  // fifo_4b_3n fifo_4b_3n_6: pin names not known
  skeleton_3x3_4b skeleton_3x3_4b_1 (
    .M_line_3(undriven_3), .M_line_1(undriven), .M_line_2(undriven_2), .clear(in_4), .enable(in_3),
    .answer(in_2), .clk(in_1), .N_column_1(undriven_4), .N_column_2(undriven_5), .N_column_3(undriven_6));  // open: S1, S2, S3
endmodule
