// Logisim project mm_3x3_4b.circ as structural Verilog: 1 circuit, main circuit mm_3x3_4b
module mm_3x3_4b (
  input  [3:0] N_column_1,
  input  [3:0] N_column_2,
  input  [3:0] N_column_3,
  input  [3:0] M_line_1,
  input  [3:0] M_line_2,
  input  [3:0] M_line_3,
  input  clear,
  input  clk,
  input  in_9
);

  wire [3:0] pe4_1_p, pe4_1_q, pe4_2_p, pe4_2_q, pe4_3_q, pe4_4_p, pe4_4_q, pe4_5_p, pe4_5_q, pe4_6_q,
       pe4_7_p, pe4_8_p;
  wire [7:0] pe4_1_s;

  pe4 pe4_1 (.M(M_line_1), .clk(clk), .clear(clear), .N(N_column_1), .P(pe4_1_p), .S(pe4_1_s), .Q(pe4_1_q));
  pe4 pe4_2 (.M(M_line_2), .clk(clk), .clear(clear), .N(pe4_1_p), .P(pe4_2_p), .Q(pe4_2_q));  // open: S
  pe4 pe4_3 (.M(M_line_3), .clk(clk), .clear(clear), .N(pe4_2_p), .Q(pe4_3_q));  // open: P, S
  pe4 pe4_4 (.M(pe4_1_q), .clk(clk), .clear(clear), .N(N_column_2), .P(pe4_4_p), .Q(pe4_4_q));  // open: S
  pe4 pe4_5 (.M(pe4_2_q), .clk(clk), .clear(clear), .N(pe4_4_p), .P(pe4_5_p), .Q(pe4_5_q));  // open: S
  pe4 pe4_6 (.M(pe4_3_q), .clk(clk), .clear(clear), .N(pe4_5_p), .Q(pe4_6_q));  // open: P, S
  pe4 pe4_7 (.M(pe4_4_q), .clk(clk), .clear(clear), .N(N_column_3), .P(pe4_7_p));  // open: S, Q
  pe4 pe4_8 (.M(pe4_5_q), .clk(clk), .clear(clear), .N(pe4_7_p), .P(pe4_8_p));  // open: S, Q
  pe4 pe4_9 (.M(pe4_6_q), .clk(clk), .clear(clear), .N(pe4_8_p));  // open: P, S, Q
endmodule
